// Logisim project ALU.circ as structural Verilog: 1 circuit, main circuit main
// ALU
module main (
  input  [31:0] ALU_SOURCE_X,
  input  [31:0] ALU_SOURCE_Y,
  input  [3:0] ALU_OPERATION,
  output LT,
  output EQ,
  output GT,
  output [31:0] ALU_RESULT,
  output ADD_OVERFLOW,
  output SUB_OVERFLOW,
  output DIV_BY_ZERO
);

  wire adder_1_cout, adder_2_cout, comparator_1_eq, comparator_2_eq, comparator_3_eq, comparator_4_gt,
       subtractor_1_bout, subtractor_2_bout, xor_1_out, xor_2_out;
  wire [31:0] Add, and_3_out, Div, divider_1_out, Mul, or_1_out, or_2_out, shifter_1_out, shifter_2_out, Sub,
       xor_3_out;

  Subtractor #(.width(32)) subtractor_1 (
    .a(ALU_SOURCE_X), .b(ALU_SOURCE_Y), .out(Sub), .bout(subtractor_1_bout));  // open: bin
  xor xor_1 (xor_1_out, subtractor_2_bout, subtractor_1_bout);
  Divider #(.width(32)) divider_1 (.a(ALU_SOURCE_X), .b(ALU_SOURCE_Y), .out(divider_1_out));  // open: upper, rem
  Comparator #(.width(32), .mode("unsigned")) comparator_1 (
    .a(ALU_SOURCE_Y), .b({32{1'b0}}), .eq(comparator_1_eq));  // open: gt, lt
  Multiplexer #(.width(32)) multiplexer_1 (
    .in0(divider_1_out), .in1(ALU_SOURCE_X), .out(Div), .sel(comparator_1_eq));  // open: en
  Subtractor #(.width(31)) subtractor_2 (
    .a(ALU_SOURCE_X[30:0]), .b(ALU_SOURCE_Y[30:0]), .bout(subtractor_2_bout));  // open: out, bin
  Comparator #(.width(4)) comparator_2 (.a(ALU_OPERATION), .b(4'b1000), .eq(comparator_2_eq));  // open: gt, lt
  Adder #(.width(32)) adder_1 (.a(ALU_SOURCE_X), .b(ALU_SOURCE_Y), .out(Add), .cout(adder_1_cout));  // open: cin
  Comparator #(.width(4), .mode("unsigned")) comparator_3 (
    .a(ALU_OPERATION), .b(4'b0111), .eq(comparator_3_eq));  // open: gt, lt
  and and_1 (SUB_OVERFLOW, xor_1_out, comparator_2_eq);
  xor xor_2 (xor_2_out, adder_2_cout, adder_1_cout);
  and and_2 (DIV_BY_ZERO, comparator_1_eq, comparator_3_eq);
  Comparator #(.width(4), .mode("unsigned")) comparator_4 (
    .a(ALU_OPERATION), .b(4'b1000), .gt(comparator_4_gt));  // open: eq, lt
  Shifter #(.width(32)) shifter_1 (.in(ALU_SOURCE_X), .\dist (ALU_SOURCE_Y[4:0]), .out(shifter_1_out));
  Shifter #(.width(32), .shift("lr")) shifter_2 (.in(ALU_SOURCE_X), .\dist (ALU_SOURCE_Y[4:0]), .out(shifter_2_out));
  assign and_3_out = ALU_SOURCE_X & ALU_SOURCE_Y;  // AND_Gate and_3, 32 bits wide
  assign or_1_out = ALU_SOURCE_X | ALU_SOURCE_Y;  // OR_Gate or_1, 32 bits wide
  assign xor_3_out = ALU_SOURCE_X ^ ALU_SOURCE_Y;  // XOR_Gate xor_3, 32 bits wide
  assign or_2_out = {{16{1'b0}}, ALU_SOURCE_X[15:0]} | {ALU_SOURCE_Y[15:0], {16{1'b0}}};  // OR_Gate or_2, 32 bits wide
  Adder #(.width(31)) adder_2 (.a(ALU_SOURCE_X[30:0]), .b(ALU_SOURCE_Y[30:0]), .cout(adder_2_cout));  // open: out, cin
  and and_4 (ADD_OVERFLOW, xor_2_out, comparator_4_gt);
  Comparator #(.width(32)) comparator_5 (.a(ALU_SOURCE_X), .b(ALU_SOURCE_Y), .gt(GT), .eq(EQ), .lt(LT));
  Multiplexer #(.select(4), .width(32)) multiplexer_2 (
    .in0(shifter_1_out), .in1(shifter_2_out), .in2(and_3_out), .in3(or_1_out), .in4(xor_3_out),
    .in5(or_2_out), .in6(Mul), .in7(Div), .in8(Sub), .in9(Add), .in10(Add), .in11(Add), .in12(Add),
    .in13(Add), .in14(Add), .in15(Add), .out(ALU_RESULT), .sel(ALU_OPERATION));  // open: en
  Multiplier #(.width(32)) multiplier_1 (.a(ALU_SOURCE_X), .b(ALU_SOURCE_Y), .out(Mul));  // open: cin, cout

  // Other names for the same wires on the sheet: X[31:0] = ALU_SOURCE_X; X2[30:0] = ALU_SOURCE_X[30:0];
  //   Y[31:0] = ALU_SOURCE_Y; Y2[30:0] = ALU_SOURCE_Y[30:0]; add_of = ADD_OVERFLOW; aluop[3:0] = ALU_OPERATION;
  //   sub_of = SUB_OVERFLOW

  // Notes on the sheet:
  //   ALU MODULE
endmodule
