// Logisim project CMP.circ as structural Verilog: 2 circuits, main circuit main
// CMP
module main (
  input  LT,
  input  EQ,
  input  GT,
  input  [2:0] CQ_QUERY,
  input  CR_WRITE,
  input  CLOCK,
  output [2:0] CR_VAL,
  output CQ_PASSED
);

  wire and_2_out, not_3_out, xnor_1_out;
  wire [2:0] and_1_out, multiplexer_1_out, multiplexer_2_out, not_1_out, register_1_q;

  Multiplexer #(.width(3)) multiplexer_1 (
    .in0(CR_VAL), .in1({LT, EQ, GT}), .out(multiplexer_1_out), .sel(CR_WRITE));  // open: en
  assign and_1_out = CQ_QUERY & CR_VAL;  // AND_Gate and_1, 3 bits wide
  Multiplexer #(.width(3)) multiplexer_2 (
    .in0(multiplexer_1_out), .in1(3'b111), .out(multiplexer_2_out), .sel(and_2_out));  // open: en
  assign not_1_out = ~multiplexer_2_out;  // NOT_Gate not_1, 3 bits wide
  or or_1 (CQ_PASSED, and_1_out[0], and_1_out[1], and_1_out[2]);
  assign CR_VAL = ~register_1_q;  // NOT_Gate not_2, 3 bits wide
  Register #(.width(3)) register_1 (.D(not_1_out), .Q(register_1_q), .clk(CLOCK));  // open: en, clr
  NotExactlyOne xnor_1 (.out(xnor_1_out), .in0(CR_VAL[0]), .in1(CR_VAL[1]), .in2(CR_VAL[2]));
  not not_3 (not_3_out, CR_WRITE);
  and and_2 (and_2_out, xnor_1_out, not_3_out);

  // Other names for the same wires on the sheet: clk = CLOCK; wenable = CR_WRITE

  // Notes on the sheet:
  //   CR MODULE
endmodule

module sub1 (
  input  [2:0] \input ,
  input  [2:0] \reg ,
  input  [2:0] constant,
  input  enable,
  input  [2:0] number,
  input  clock,
  output [2:0] reg_2
);

  wire and_1_out;
  wire [2:0] multiplexer_1_out, multiplexer_2_out, xnor_1_out;

  assign xnor_1_out = ~(constant ^ number);  // XNOR_Gate xnor_1, 3 bits wide
  and and_1 (and_1_out, xnor_1_out[0], xnor_1_out[1], xnor_1_out[2]);
  Multiplexer #(.width(3)) multiplexer_1 (
    .in0(\reg ), .in1(\input ), .out(multiplexer_1_out), .sel(and_1_out));  // open: en
  Multiplexer #(.width(3)) multiplexer_2 (
    .in0(\reg ), .in1(multiplexer_1_out), .out(multiplexer_2_out), .sel(enable));  // open: en
  Register #(.width(3)) register_1 (.D(multiplexer_2_out), .Q(reg_2), .clk(clock));  // open: en, clr
endmodule
