// Logisim project CPU.circ as structural Verilog: 2 circuits, main circuit main
// CPU
module main (
  input  [31:0] INSTRUCTION,
  input  [23:0] CURRENT_PC,
  input  CQ_PASSED,
  input  [31:0] REG_1_VAL,
  input  [31:0] REG_2_VAL,
  input  [31:0] REG_3_VAL,
  input  [31:0] ALU_RESULT,
  input  [31:0] MEM_OUT,
  output [23:0] JUMP_ADDRESS,
  output [2:0] CQ_QUERY,
  output CR_WRITE,
  output [3:0] REG_1_READ,
  output [3:0] REG_2_READ,
  output [3:0] REG_3_WRITE,
  output [31:0] REG_WRITE_VAL,
  output REG_WRITE,
  output [31:0] ALU_SOURCE_X,
  output [31:0] ALU_SOURCE_Y,
  output [3:0] ALU_OPERATION,
  output [23:0] MEM_ADDR,
  output [31:0] MEM_IN,
  output MEM_WRITE
);

  wire imm_mark, JMP, LNK, mem_read, SET_LOW, SUB;
  wire [15:0] control_signal_ri_16;
  wire [19:0] control_signal_ri_20;
  wire [23:0] bit_extender_1_out, jmp_addr_imm;
  wire [31:0] bit_extender_2_out, I16_ext, I20_ext, multiplexer_2_out, multiplexer_3_out, multiplexer_4_out,
       multiplexer_5_out, multiplexer_6_out, multiplexer_7_out, multiplexer_8_out, multiplexer_10_out, PC_ext;

  Bit_Extender #(.in_width(32), .out_width(24)) bit_extender_1 (.in(REG_2_VAL), .out(bit_extender_1_out));
  Multiplexer #(.width(24), .enable("false")) multiplexer_1 (
    .in0(bit_extender_1_out), .in1(jmp_addr_imm), .out(JUMP_ADDRESS), .sel(imm_mark));
  assign bit_extender_2_out = {{8{CURRENT_PC[23]}}, CURRENT_PC};  // Bit_Extender bit_extender_2
  Multiplexer #(.width(32), .enable("false")) multiplexer_2 (
    .in0(REG_2_VAL), .in1(I20_ext), .out(multiplexer_2_out), .sel(imm_mark));
  Bit_Extender #(.in_width(32), .out_width(24)) bit_extender_3 (.in(ALU_RESULT), .out(MEM_ADDR));
  Multiplexer #(.width(32), .enable("false")) multiplexer_3 (
    .in0({32{1'b0}}), .in1(INSTRUCTION), .out(multiplexer_3_out), .sel(CQ_PASSED));
  Subtractor #(.width(32)) subtractor_1 (.a(bit_extender_2_out), .b(32'h1), .out(PC_ext));  // open: bin, bout
  Multiplexer #(.width(32), .enable("false")) multiplexer_4 (
    .in0(REG_1_VAL), .in1(REG_3_VAL), .out(multiplexer_4_out), .sel(CR_WRITE));
  Multiplexer #(.width(32), .enable("false")) multiplexer_5 (
    .in0(ALU_RESULT), .in1(multiplexer_2_out), .out(multiplexer_5_out), .sel(SET_LOW));
  Multiplexer #(.width(32), .enable("false")) multiplexer_6 (
    .in0(REG_2_VAL), .in1(I16_ext), .out(multiplexer_6_out), .sel(imm_mark));
  Multiplexer #(.width(32), .enable("false")) multiplexer_7 (
    .in0(multiplexer_4_out), .in1(multiplexer_6_out), .out(multiplexer_7_out), .sel(SUB));
  Multiplexer #(.width(32), .enable("false")) multiplexer_8 (
    .in0(I16_ext), .in1(REG_1_VAL), .out(multiplexer_8_out), .sel(SUB));
  control_center control_signal (
    .instru(multiplexer_3_out), .alu_op(ALU_OPERATION), .imm_mark(imm_mark), .ri_20(control_signal_ri_20),
    .cr_write___cmp(CR_WRITE), .sub_mark(SUB), .ri(REG_2_READ), .Lnk_mark(LNK), .ri_16(control_signal_ri_16),
    .rs(REG_1_READ), .jmp_addr(jmp_addr_imm), .rd(REG_3_WRITE), .i0_mark___jmp(JMP),
    .set_lower_mark(SET_LOW), .mem_read_mark(mem_read), .mem_write_mark(MEM_WRITE), .reg_write_mark(REG_WRITE));  // open: cr, i1_mark
  Multiplexer #(.width(32), .enable("false")) multiplexer_9 (
    .in0(multiplexer_7_out), .in1(PC_ext), .out(ALU_SOURCE_X), .sel(LNK));
  Multiplexer #(.width(32), .enable("false")) multiplexer_10 (
    .in0(multiplexer_8_out), .in1(I20_ext), .out(multiplexer_10_out), .sel(LNK));
  Multiplexer #(.width(32), .enable("false")) multiplexer_11 (
    .in0(multiplexer_5_out), .in1(MEM_OUT), .out(REG_WRITE_VAL), .sel(mem_read));
  assign I20_ext = {{12{control_signal_ri_20[19]}}, control_signal_ri_20};  // Bit_Extender bit_extender_4
  Multiplexer #(.width(32), .enable("false")) multiplexer_12 (
    .in0(REG_2_VAL), .in1(multiplexer_10_out), .out(ALU_SOURCE_Y), .sel(imm_mark));
  assign I16_ext = {{16{control_signal_ri_16[15]}}, control_signal_ri_16};  // Bit_Extender bit_extender_5

  assign CQ_QUERY = INSTRUCTION[27:25];
  assign MEM_IN = REG_3_VAL;

  // Other names for the same wires on the sheet: alu_op[3:0] = ALU_OPERATION; CMP = CR_WRITE;
  //   cr_q[2:0] = INSTRUCTION[27:25]; instru_a[31:0] = INSTRUCTION; Imm_from_reg[31:0] = REG_2_VAL;
  //   Mem_read_val[31:0] = MEM_OUT; For_Cmp[31:0] = REG_3_VAL; Mem_St[31:0] = REG_3_VAL; RD[3:0] = REG_3_WRITE;
  //   read_to_reg[31:0] = REG_WRITE_VAL; RI[3:0] = REG_2_READ; RS[3:0] = REG_1_READ; RS_VAL[31:0] = REG_1_VAL;
  //   X[31:0] = ALU_SOURCE_X; Y[31:0] = ALU_SOURCE_Y

  // Notes on the sheet:
  //   INSTRUCTION MODULE
  //   CR MODULE
  //   REGISTER FILE MODULE
  //   ALU MODULE
  //   MEMORY MODULE
endmodule

module control_center (
  input  [31:0] instru,
  output cr_write___cmp,
  output sub_mark,
  output [3:0] ri,
  output Lnk_mark,
  output [15:0] ri_16,
  output [3:0] rs,
  output [23:0] jmp_addr,
  output [3:0] rd,
  output i0_mark___jmp,
  output i1_mark,
  output set_lower_mark,
  output [19:0] ri_20,
  output mem_read_mark,
  output [3:0] alu_op,
  output mem_write_mark,
  output imm_mark,
  output [2:0] cr,
  output reg_write_mark
);

  wire comparator_4_gt, comparator_9_eq, comparator_10_eq, comparator_11_eq, comparator_12_eq,
       comparator_13_lt, or_1_out;

  Comparator #(.width(4), .mode("unsigned")) comparator_1 (
    .a(instru[31:28]), .b(4'b1101), .eq(cr_write___cmp));  // open: gt, lt
  Comparator #(.width(4), .mode("unsigned")) comparator_2 (
    .a(instru[31:28]), .b(4'b1000), .eq(sub_mark));  // open: gt, lt
  Comparator #(.width(4), .mode("unsigned")) comparator_3 (
    .a(instru[31:28]), .b(4'b1110), .eq(Lnk_mark));  // open: gt, lt
  Comparator #(.width(4), .mode("unsigned")) comparator_4 (.b(instru[31:28]), .gt(comparator_4_gt));  // open: a, eq, lt
  Comparator #(.width(4), .mode("unsigned")) comparator_5 (
    .a(instru[31:28]), .b(4'b1111), .eq(i0_mark___jmp));  // open: gt, lt
  Comparator #(.width(4), .mode("unsigned")) comparator_6 (
    .a(instru[31:28]), .b(4'b1100), .eq(set_lower_mark));  // open: gt, lt
  Comparator #(.width(4), .mode("unsigned")) comparator_7 (
    .a(instru[31:28]), .b(4'b1010), .eq(mem_read_mark));  // open: gt, lt
  Comparator #(.width(4), .mode("unsigned")) comparator_8 (
    .a(instru[31:28]), .b(4'b1011), .eq(mem_write_mark));  // open: gt, lt
  Comparator #(.width(4), .mode("unsigned")) comparator_9 (
    .a(instru[31:28]), .b(4'b1111), .eq(comparator_9_eq));  // open: gt, lt
  Comparator #(.width(4), .mode("unsigned")) comparator_10 (
    .a(instru[31:28]), .b(4'b1011), .eq(comparator_10_eq));  // open: gt, lt
  Comparator #(.width(4), .mode("unsigned")) comparator_11 (
    .a(instru[31:28]), .b(4'b1101), .eq(comparator_11_eq));  // open: gt, lt
  Comparator #(.width(32), .mode("unsigned")) comparator_12 (
    .a(instru), .b({32{1'b0}}), .eq(comparator_12_eq));  // open: gt, lt
  Comparator #(.width(4), .mode("unsigned")) comparator_13 (
    .a(instru[31:28]), .b(4'b1111), .lt(comparator_13_lt));  // open: gt, eq
  or or_1 (or_1_out, comparator_9_eq, comparator_10_eq, comparator_11_eq, comparator_12_eq);
  and and_1 (i1_mark, comparator_4_gt, comparator_13_lt);
  not not_1 (reg_write_mark, or_1_out);

  assign alu_op = instru[31:28];
  assign cr = instru[27:25];
  assign imm_mark = instru[24];
  assign jmp_addr = instru[23:0];
  assign rd = instru[23:20];
  assign ri = instru[3:0];
  assign ri_16 = instru[15:0];
  assign ri_20 = instru[19:0];
  assign rs = instru[19:16];

  // Other names for the same wires on the sheet: instruction[31:0] = instru; opcode[3:0] = instru[31:28]
endmodule
