// Logisim project NPC.circ as structural Verilog: 1 circuit, main circuit main
// NPC
module main (
  input  CQ_PASSED,
  input  [31:0] INSTRUCTION,
  input  [23:0] CURRENT_PC,
  input  [23:0] JUMP_ADDRESS,
  output [23:0] NEXT_PC
);

  wire and_1_out;
  wire [3:0] xnor_1_out;
  wire [23:0] adder_1_out;

  Adder #(.width(24)) adder_1 (.a(24'h1), .b(CURRENT_PC), .out(adder_1_out));  // open: cin, cout
  assign xnor_1_out = ~(4'b1111 ^ INSTRUCTION[31:28]);  // XNOR_Gate xnor_1, 4 bits wide
  and and_1 (and_1_out, CQ_PASSED, xnor_1_out[0], xnor_1_out[1], xnor_1_out[2], xnor_1_out[3]);
  Multiplexer #(.width(24)) multiplexer_1 (
    .in0(adder_1_out), .in1(JUMP_ADDRESS), .out(NEXT_PC), .sel(and_1_out));  // open: en

  // Notes on the sheet:
  //   NPC MODULE
endmodule
