// Logisim project PIP.circ as structural Verilog: 1 circuit, main circuit main
// PIP
module main (
  input  CQ_PASSED,
  input  [31:0] INSTRUCTION_IN,
  input  [23:0] PC_IN,
  input  CLOCK,
  output [31:0] INSTRUCTION_OUT,
  output [23:0] PC_OUT
);

  wire and_1_out, and_2_out, register_1_q, register_3_q;
  wire [3:0] xnor_1_out;
  wire [31:0] register_2_q;

  Register #(.width(1)) register_1 (.D(CQ_PASSED), .Q(register_1_q), .clk(CLOCK));  // open: en, clr
  Register #(.width(32)) register_2 (.D(INSTRUCTION_IN), .Q(register_2_q), .clk(CLOCK));  // open: en, clr
  and and_1 (and_1_out, register_1_q, register_3_q);
  Register #(.width(1)) register_3 (.D(and_2_out), .Q(register_3_q), .clk(CLOCK));  // open: en, clr
  and and_2 (and_2_out, xnor_1_out[0], xnor_1_out[1], xnor_1_out[2], xnor_1_out[3]);
  Multiplexer #(.width(32)) multiplexer_1 (
    .in0(register_2_q), .in1({32{1'b0}}), .out(INSTRUCTION_OUT), .sel(and_1_out));  // open: en
  assign xnor_1_out = ~(register_2_q[31:28] ^ 4'b1111);  // XNOR_Gate xnor_1, 4 bits wide

  assign PC_OUT = PC_IN;

  // Other names for the same wires on the sheet: clk = CLOCK; CQ = CQ_PASSED; instru[31:0] = INSTRUCTION_IN

  // Notes on the sheet:
  //   PIPELINE MODULE
endmodule
