// Logisim project REG.circ as structural Verilog: 1 circuit, main circuit main
// REG
module main (
  input  CLOCK,
  input  [3:0] REG_1_READ,
  input  [3:0] REG_2_READ,
  input  [3:0] REG_3_WRITE,
  input  [31:0] REG_WRITE_VAL,
  input  REG_WRITE,
  output [31:0] R00,
  output [31:0] R01,
  output [31:0] R02,
  output [31:0] R03,
  output [31:0] R04,
  output [31:0] R05,
  output [31:0] R06,
  output [31:0] R07,
  output [31:0] REG_1_VAL,
  output [31:0] REG_2_VAL,
  output [31:0] REG_3_VAL,
  output [31:0] R08,
  output [31:0] R09,
  output [31:0] R10,
  output [31:0] R11,
  output [31:0] R12,
  output [31:0] R13,
  output [31:0] R14,
  output [31:0] R15
);

  wire R00_e, R01_e, R02_e, R03_e, R04_e, R05_e, R06_e, R07_e, R08_e, R09_e, R10_e, R11_e, R12_e, R13_e,
       R14_e, R15_e;
  wire [31:0] R00_i, R00_v, R01_i, R01_v, R02_i, R02_v, R03_i, R03_v, R04_i, R04_v, R05_i, R05_v, R06_i,
       R06_v, R07_i, R07_v, R08_i, R08_v, R09_i, R09_v, R10_i, R10_v, R11_i, R11_v, R12_i, R12_v, R13_i,
       R13_v, R14_i, R14_v, R15_i, R15_v;

  Multiplexer #(.width(32)) multiplexer_1 (.in0(R00), .in1(R00_v), .out(R00_i), .sel(R00_e));  // open: en
  Multiplexer #(.width(32)) multiplexer_2 (.in0(R05), .in1(R05_v), .out(R05_i), .sel(R05_e));  // open: en
  Multiplexer #(.width(32)) multiplexer_3 (.in0(R10), .in1(R10_v), .out(R10_i), .sel(R10_e));  // open: en
  Multiplexer #(.width(32)) multiplexer_4 (.in0(R15), .in1(R15_v), .out(R15_i), .sel(R15_e));  // open: en
  Demultiplexer #(.select(4), .width(32)) demultiplexer_1 (
    .out0(R00_v), .out1(R01_v), .out2(R02_v), .out3(R03_v), .out4(R04_v), .out5(R05_v), .out6(R06_v),
    .out7(R07_v), .out8(R08_v), .out9(R09_v), .out10(R10_v), .out11(R11_v), .out12(R12_v), .out13(R13_v),
    .out14(R14_v), .out15(R15_v), .in(REG_WRITE_VAL), .sel(REG_3_WRITE), .en(REG_WRITE));
  Demultiplexer #(.select(4)) demultiplexer_2 (
    .out0(R00_e), .out1(R01_e), .out2(R02_e), .out3(R03_e), .out4(R04_e), .out5(R05_e), .out6(R06_e),
    .out7(R07_e), .out8(R08_e), .out9(R09_e), .out10(R10_e), .out11(R11_e), .out12(R12_e), .out13(R13_e),
    .out14(R14_e), .out15(R15_e), .in(1'b1), .sel(REG_3_WRITE));  // open: en
  Register #(.width(32)) register_1 (.D(R05_i), .Q(R05), .clk(CLOCK));  // open: en, clr
  Register #(.width(32)) register_2 (.D(R06_i), .Q(R06), .clk(CLOCK));  // open: en, clr
  Register #(.width(32)) register_3 (.D(R12_i), .Q(R12), .clk(CLOCK));  // open: en, clr
  Multiplexer #(.width(32)) multiplexer_5 (.in0(R01), .in1(R01_v), .out(R01_i), .sel(R01_e));  // open: en
  Multiplexer #(.width(32)) multiplexer_6 (.in0(R06), .in1(R06_v), .out(R06_i), .sel(R06_e));  // open: en
  Multiplexer #(.width(32)) multiplexer_7 (.in0(R11), .in1(R11_v), .out(R11_i), .sel(R11_e));  // open: en
  Register #(.width(32)) register_4 (.D(R00_i), .Q(R00), .clk(CLOCK));  // open: en, clr
  Register #(.width(32)) register_5 (.D(R07_i), .Q(R07), .clk(CLOCK));  // open: en, clr
  Register #(.width(32)) register_6 (.D(R13_i), .Q(R13), .clk(CLOCK));  // open: en, clr
  Multiplexer #(.width(32)) multiplexer_8 (.in0(R02), .in1(R02_v), .out(R02_i), .sel(R02_e));  // open: en
  Multiplexer #(.width(32)) multiplexer_9 (.in0(R07), .in1(R07_v), .out(R07_i), .sel(R07_e));  // open: en
  Multiplexer #(.width(32)) multiplexer_10 (.in0(R12), .in1(R12_v), .out(R12_i), .sel(R12_e));  // open: en
  Register #(.width(32)) register_7 (.D(R01_i), .Q(R01), .clk(CLOCK));  // open: en, clr
  Register #(.width(32)) register_8 (.D(R08_i), .Q(R08), .clk(CLOCK));  // open: en, clr
  Register #(.width(32)) register_9 (.D(R14_i), .Q(R14), .clk(CLOCK));  // open: en, clr
  Multiplexer #(.select(4), .width(32)) multiplexer_11 (
    .in0(R00), .in1(R01), .in2(R02), .in3(R03), .in4(R04), .in5(R05), .in6(R06), .in7(R07), .in8(R08),
    .in9(R09), .in10(R10), .in11(R11), .in12(R12), .in13(R13), .in14(R14), .in15(R15), .out(REG_2_VAL),
    .sel(REG_2_READ));  // open: en
  Register #(.width(32)) register_10 (.D(R02_i), .Q(R02), .clk(CLOCK));  // open: en, clr
  Register #(.width(32)) register_11 (.D(R09_i), .Q(R09), .clk(CLOCK));  // open: en, clr
  Register #(.width(32)) register_12 (.D(R15_i), .Q(R15), .clk(CLOCK));  // open: en, clr
  Multiplexer #(.width(32)) multiplexer_12 (.in0(R03), .in1(R03_v), .out(R03_i), .sel(R03_e));  // open: en
  Multiplexer #(.width(32)) multiplexer_13 (.in0(R08), .in1(R08_v), .out(R08_i), .sel(R08_e));  // open: en
  Multiplexer #(.width(32)) multiplexer_14 (.in0(R13), .in1(R13_v), .out(R13_i), .sel(R13_e));  // open: en
  Multiplexer #(.select(4), .width(32)) multiplexer_15 (
    .in0(R00), .in1(R01), .in2(R02), .in3(R03), .in4(R04), .in5(R05), .in6(R06), .in7(R07), .in8(R08),
    .in9(R09), .in10(R10), .in11(R11), .in12(R12), .in13(R13), .in14(R14), .in15(R15), .out(REG_3_VAL),
    .sel(REG_3_WRITE));  // open: en
  Register #(.width(32)) register_13 (.D(R03_i), .Q(R03), .clk(CLOCK));  // open: en, clr
  Register #(.width(32)) register_14 (.D(R10_i), .Q(R10), .clk(CLOCK));  // open: en, clr
  Multiplexer #(.width(32)) multiplexer_16 (.in0(R04), .in1(R04_v), .out(R04_i), .sel(R04_e));  // open: en
  Multiplexer #(.width(32)) multiplexer_17 (.in0(R09), .in1(R09_v), .out(R09_i), .sel(R09_e));  // open: en
  Multiplexer #(.width(32)) multiplexer_18 (.in0(R14), .in1(R14_v), .out(R14_i), .sel(R14_e));  // open: en
  Multiplexer #(.select(4), .width(32)) multiplexer_19 (
    .in0(R00), .in1(R01), .in2(R02), .in3(R03), .in4(R04), .in5(R05), .in6(R06), .in7(R07), .in8(R08),
    .in9(R09), .in10(R10), .in11(R11), .in12(R12), .in13(R13), .in14(R14), .in15(R15), .out(REG_1_VAL),
    .sel(REG_1_READ));  // open: en
  Register #(.width(32)) register_15 (.D(R04_i), .Q(R04), .clk(CLOCK));  // open: en, clr
  Register #(.width(32)) register_16 (.D(R11_i), .Q(R11), .clk(CLOCK));  // open: en, clr

  // Other names for the same wires on the sheet: clk = CLOCK; wenable = REG_WRITE

  // Notes on the sheet:
  //   REGISTER FILE MODULE
endmodule
